# Fritzing sketch circuit-diagram (saved by Fritzing 0.9.6b)

parts:
  U1 = NodeMCU V3.0
  S1 = Pushbutton [package="[THT]"]
  Power_plug1 = Power plug
  S2 = H-Bridge with L298N
  M1 = Stepper Motor - Bipolar

nets:
  N1: U1.D1, S2.IN1
  N2: U1.D2, S2.IN2
  N3: U1.D3, S2.IN3
  N4: U1.D4, S2.IN4
  GND: U1.GND, Power_plug1.GND, S2.GND
  VIN: U1.Vin, S2.5V
  VCC: S1.Pin_3, S1.Pin_4, Power_plug1.VCC, S2.12V
  N5: S2.M1-01, M1.C
  N6: S2.M1-02, M1.A
  N7: S2.M2-01, M1.D
  N8: S2.M2-02, M1.B

custom parts:
  NodeMCU V3.0: ESP8266 based NodeMCU
  H-Bridge with L298N: h-bridge
